// Logisim project 8to1_multiplexor.circ as structural Verilog: 1 circuit, main circuit main
module main (
);

  wire and_1_out, and_2_out, and_3_out, and_4_out, and_5_out, and_6_out, and_7_out, and_8_out,
       dipswitch_1_p1, dipswitch_1_p2, dipswitch_1_p3, dipswitch_2_p1, dipswitch_2_p2, dipswitch_2_p3,
       dipswitch_2_p4, dipswitch_2_p5, dipswitch_2_p6, dipswitch_2_p7, dipswitch_2_p8, not_1_out, not_2_out,
       not_3_out, or_1_out;

  // DipSwitch dipswitch_1: pin names not known; wires that end beside it: dipswitch_1_p1, dipswitch_1_p2, dipswitch_1_p3
  // DipSwitch dipswitch_2: pin names not known; wires that end beside it: dipswitch_2_p1, dipswitch_2_p2, dipswitch_2_p3, dipswitch_2_p4, dipswitch_2_p5, dipswitch_2_p6, dipswitch_2_p7, dipswitch_2_p8
  not not_1 (not_1_out, dipswitch_1_p3);
  not not_2 (not_2_out, dipswitch_1_p2);
  not not_3 (not_3_out, dipswitch_1_p1);
  and and_1 (and_1_out, not_1_out, not_2_out, not_3_out, dipswitch_2_p1);
  and and_2 (and_2_out, dipswitch_1_p1, not_2_out, not_1_out, dipswitch_2_p2);
  and and_3 (and_3_out, dipswitch_1_p2, not_3_out, not_1_out, dipswitch_2_p3);
  and and_4 (and_4_out, dipswitch_1_p2, dipswitch_1_p1, not_1_out, dipswitch_2_p4);
  and and_5 (and_5_out, dipswitch_1_p3, not_2_out, not_3_out, dipswitch_2_p5);
  and and_6 (and_6_out, dipswitch_1_p3, dipswitch_1_p1, not_2_out, dipswitch_2_p6);
  and and_7 (and_7_out, dipswitch_1_p3, not_3_out, dipswitch_1_p2, dipswitch_2_p7);
  and and_8 (and_8_out, dipswitch_1_p3, dipswitch_1_p1, dipswitch_1_p2, dipswitch_2_p8);
  or or_1 (or_1_out, and_1_out, and_2_out, and_3_out, and_4_out, and_5_out, and_6_out, and_7_out, and_8_out);
  LED led_1 (.in(or_1_out));
endmodule
