// Logisim project 8to3_encoder.circ as structural Verilog: 1 circuit, main circuit main
module main (
);

  wire dipswitch_1_p1, dipswitch_1_p2, dipswitch_1_p3, dipswitch_1_p4, dipswitch_1_p5, dipswitch_1_p6,
       dipswitch_1_p7, or_1_out, or_2_out, or_3_out;

  // DipSwitch dipswitch_1: pin names not known; wires that end beside it: dipswitch_1_p1, dipswitch_1_p2, dipswitch_1_p3, dipswitch_1_p4, dipswitch_1_p5, dipswitch_1_p6, dipswitch_1_p7
  or or_1 (or_1_out, dipswitch_1_p1, dipswitch_1_p3, dipswitch_1_p5, dipswitch_1_p7);
  or or_2 (or_2_out, dipswitch_1_p2, dipswitch_1_p3, dipswitch_1_p6, dipswitch_1_p7);
  or or_3 (or_3_out, dipswitch_1_p4, dipswitch_1_p5, dipswitch_1_p6, dipswitch_1_p7);
  LED led_1 (.in(or_1_out));
  LED led_2 (.in(or_2_out));
  LED led_3 (.in(or_3_out));
endmodule
