// Logisim project half_adder.circ as structural Verilog: 1 circuit, main circuit main
module main (
);

  wire and_1_out, dipswitch_1_sw1, dipswitch_1_sw2, xor_1_out;

  DipSwitch dipswitch_1 (.sw1(dipswitch_1_sw1), .sw2(dipswitch_1_sw2));  // open: sw3, sw4, sw5, sw6, sw7, sw8
  xor xor_1 (xor_1_out, dipswitch_1_sw1, dipswitch_1_sw2);
  and and_1 (and_1_out, dipswitch_1_sw1, dipswitch_1_sw2);
  // Digital_Oscilloscope digital_oscilloscope_1: pin names not known; wires that end beside it: xor_1_out, dipswitch_1_sw1, dipswitch_1_sw2, and_1_out
endmodule
